# Fritzing sketch board (saved by Fritzing 0.9.10b)
breadboards: 1

parts:
  U2 = LIPO-1000mAh [package=lipo-1000]  # not connected
  M1 = Max30205 body temp sensor [package=THT]
  Boron1 = Particle Boron
  LED1 = RGB LED (com. anode, rbg) [package="5 mm [THT]"]

nets:
  VCC: M1.VCC, Boron1.3.3V
  GND: M1.GND, M1.A0, M1.A1, M1.A2, Boron1.GND, LED1.common_anode
  N1: M1.SDA, Boron1.SDA
  N2: M1.SCL, Boron1.SCL
  N3: Boron1.A0, LED1.red_cathode
  N4: Boron1.A1, LED1.blue_cathode
  N5: Boron1.A2, LED1.green_cathode

custom parts:
  Max30205 body temp sensor: This module is based on MAX30205 which is a temperature sensor that accurately measures temperature and provides an over-temperature alarm/interrupt/shutdown output.
  Particle Boron: The Boron LTE is a powerful LTE CAT-M1 enabled development kit that can act as either a standalone cellular device or LTE enabled gateway, repeater, or endpoint for a Particle Mesh networks. Equipped with the Nordic nRF52840 and u-blox SARA 410 processors, the Boron has built-in battery charging circuitry which makes it easier to connect a Li-Po battery and 20 mixed signal GPIOs to interface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
